// Logisim project 13456938_ass4ALU.circ as structural Verilog: 1 circuit, main circuit main
module main (
  input  [7:0] in_1,
  input  [7:0] in_2,
  input  Enable,
  input  in_4
);

  wire [7:0] adder_1_out, demultiplexer_1_out0, demultiplexer_1_out1, multiplexer_1_out, xor_1_out;

  Demultiplexer #(.width(8)) demultiplexer_1 (
    .out0(demultiplexer_1_out0), .out1(demultiplexer_1_out1), .in(in_2), .sel(in_4), .en(Enable));
  assign xor_1_out = demultiplexer_1_out1 ^ {8{1'b1}};  // XOR_Gate xor_1, 8 bits wide
  Multiplexer #(.width(8)) multiplexer_1 (
    .in0(demultiplexer_1_out0), .in1(xor_1_out), .out(multiplexer_1_out), .sel(in_4), .en(Enable));
  Adder adder_1 (.a(in_1), .b(multiplexer_1_out), .out(adder_1_out), .cin(in_4));  // open: cout
  Hex_Digit_Display hex_digit_display_1 (.value(adder_1_out[7:4]));  // open: dp
  Hex_Digit_Display hex_digit_display_2 (.value(adder_1_out[3:0]));  // open: dp

  // Notes on the sheet:
  //   binary value A
  //   binary value B
  //   Addition 0/ Subtraction 1
  //   demultiplexer
  //   block to turn number negative if mux and demux select bits are 1
  //   multiplexer
  //   8 bitAdder
  //   Output
endmodule
