// Logisim project 13456938_ass4PC&ROM.circ as structural Verilog: 1 circuit, main circuit main
module main (
  input  Enable,
  input  Reset
);

  wire Clock_out;
  wire [5:0] register_1_q;
  wire [7:0] adder_1_out;
  wire [11:0] rom_1_data;

  Clock Clock (.out(Clock_out));
  Register register_1 (
    .D(adder_1_out), .en(Enable), .Q({register_1_q, adder_1_out[1:0]}), .clk(Clock_out), .clr(Reset));
  Adder #(.width(6)) adder_1 (.a(register_1_q), .b(6'b000001), .out(adder_1_out[7:2]));  // open: cin, cout
  ROM #(.addrWidth(6), .dataWidth(12)) rom_1 (.addr(register_1_q), .data(rom_1_data));  // open: sel
  LED led_1 (.in(rom_1_data[0]));
  LED led_2 (.in(rom_1_data[1]));
  LED led_3 (.in(rom_1_data[2]));
  LED led_4 (.in(rom_1_data[3]));
  LED led_5 (.in(rom_1_data[4]));
  LED led_6 (.in(rom_1_data[5]));
  LED led_7 (.in(rom_1_data[6]));
  LED led_8 (.in(rom_1_data[7]));
  LED led_9 (.in(rom_1_data[8]));
  LED led_10 (.in(rom_1_data[9]));
  LED led_11 (.in(rom_1_data[10]));
  LED led_12 (.in(rom_1_data[11]));

  // Notes on the sheet:
  //   Combining 2 LSBs and 6 MSBs +4
  //   6 MSBs
  //   2 LSBs
  //   8bit register
  //   Splitting out put into 2 LSBs and 6 MSBs
  //   6bit adder
  //   ROM 6Abit 12 Dbit
  //   contents of rom_1 (hex, n*v repeats v):
  //   60 1b4 212 393 4c2
  //   LSB
  //   OUTPUT
  //   MSB
endmodule
