// Logisim project 13456938_ass4PC.circ as structural Verilog: 1 circuit, main circuit main
module main (
  input  Enable,
  input  Reset
);

  wire Clock_out;
  wire [5:0] _8bit_Register_q;
  wire [7:0] adder_1_out;

  Clock Clock (.out(Clock_out));
  Register _8bit_Register (
    .D(adder_1_out), .en(Enable), .Q({_8bit_Register_q, adder_1_out[1:0]}), .clk(Clock_out), .clr(Reset));
  Adder #(.width(6)) adder_1 (.a(_8bit_Register_q), .b(6'b000001), .out(adder_1_out[7:2]));  // open: cin, cout
  LED led_1 (.in(adder_1_out[0]));
  LED led_2 (.in(adder_1_out[1]));
  LED led_3 (.in(_8bit_Register_q[0]));
  LED led_4 (.in(_8bit_Register_q[1]));
  LED led_5 (.in(_8bit_Register_q[2]));
  LED led_6 (.in(_8bit_Register_q[3]));
  LED led_7 (.in(_8bit_Register_q[4]));
  LED led_8 (.in(_8bit_Register_q[5]));

  // Notes on the sheet:
  //   Combining 2 LSBs and 6 MSBs +4
  //   2 LSBs
  //   6 MSBs
  //   Add 1 to 6 MSBs (ie +4)
  //   Splitting out put into 2 LSBs and 6 MSBs
  //   6bit Adder
  //   LSB
  //   MSB
  //   Output
endmodule
