// Logisim project ALU.circ as structural Verilog: 1 circuit, main circuit main
module main (
  input  [7:0] A,
  input  [7:0] B,
  input  Enable,
  input  Add_Sub,
  output [7:0] Output
);

  wire [7:0] demultiplexer_1_out0, demultiplexer_1_out1, multiplexer_1_out, xor_1_out;

  Demultiplexer #(.width(8)) demultiplexer_1 (
    .out0(demultiplexer_1_out0), .out1(demultiplexer_1_out1), .in(B), .sel(Add_Sub), .en(Enable));
  assign xor_1_out = demultiplexer_1_out1 ^ {8{1'b1}};  // XOR_Gate xor_1, 8 bits wide
  Multiplexer #(.width(8)) multiplexer_1 (
    .in0(demultiplexer_1_out0), .in1(xor_1_out), .out(multiplexer_1_out), .sel(Add_Sub), .en(Enable));
  Adder adder_1 (.a(A), .b(multiplexer_1_out), .out(Output), .cin(Add_Sub));  // open: cout
  Hex_Digit_Display hex_digit_display_1 (.value(Output[7:4]));  // open: dp
  Hex_Digit_Display hex_digit_display_2 (.value(Output[3:0]));  // open: dp

  // Notes on the sheet:
  //   demultiplexer
  //   block to turn number negative if mux and demux select bits are 1
  //   multiplexer
  //   8 bitAdder
  //   Output
endmodule
