// Logisim project PC.circ as structural Verilog: 1 circuit, main circuit main
module main (
  input  Enable,
  input  Reset
);

  wire Clock_out;
  wire [7:0] _8bit_Register_q, adder_1_out;

  Clock Clock (.out(Clock_out));
  Register _8bit_Register (.D(adder_1_out), .en(Enable), .Q(_8bit_Register_q), .clk(Clock_out), .clr(Reset));
  Adder adder_1 (.a(_8bit_Register_q), .b(8'h1), .out(adder_1_out));  // open: cin, cout
endmodule
