// Logisim project 13456938_a5q1.circ as structural Verilog: 5 circuits, main circuit main
// ALU
module main (
  input  Reset_PC,
  input  enable,
  input  clear,
  output [7:0] rd,
  output [3:0] rd_offset_constant,
  output [7:0] rs,
  output [1:0] out_7,
  output [1:0] out_8,
  output [7:0] out_9,
  output [7:0] rt,
  output [1:0] out_11
);

  wire clock_1_out, control_1_add_sub, control_1_alu___mem, control_1_alusrc, control_1_memread__lw,
       control_1_memwrite, control_1_regwrite__sw;
  wire [7:0] bit_extender_1_out, multiplexer_2_out, pc_1_output, ram_1_data;
  wire [11:0] rom_1_data;

  Clock clock_1 (.out(clock_1_out));
  PC pc_1 (.Enable(enable), .Reset(Reset_PC), .Clock(clock_1_out), .Output(pc_1_output));
  ROM #(.dataWidth(12)) rom_1 (.addr(pc_1_output), .data(rom_1_data), .sel(enable));
  control control_1 (
    .\input (rom_1_data), .RegWrite__sw(control_1_regwrite__sw), .ALU___mem(control_1_alu___mem),
    .MemRead__lw(control_1_memread__lw), .Add_Sub(control_1_add_sub), .ALUSrc(control_1_alusrc), .rs(out_8),
    .rt(out_11), .rd_offset_constant(rd_offset_constant), .destination(out_7), .MemWrite(control_1_memwrite));
  Multiplexer #(.width(8)) multiplexer_1 (
    .in0(ram_1_data), .in1(out_9), .out(rd), .sel(control_1_alu___mem), .en(enable));
  register register_1 (
    .WriteData(rd), .WriteReg(out_7), .RegWrite(control_1_regwrite__sw), .Clock(clock_1_out), .ReadData1(rs),
    .ReadReg1(out_8), .ReadData2(rt), .ReadReg2(out_11));
  assign bit_extender_1_out = {{4{rd_offset_constant[3]}}, rd_offset_constant};  // Bit_Extender bit_extender_1
  ALU alu_1 (.A(rs), .B(multiplexer_2_out), .Enable(enable), .Add_Sub(control_1_add_sub), .Output(out_9));
  Multiplexer #(.width(8)) multiplexer_2 (
    .in0(rt), .in1(bit_extender_1_out), .out(multiplexer_2_out), .sel(control_1_alusrc), .en(enable));
  RAM #(.bus("separate")) ram_1 (
    .addr(out_9), .din(rt), .data(ram_1_data), .str(control_1_memwrite), .sel(enable), .clk(clock_1_out),
    .ld(control_1_memread__lw), .clr(clear));

  // Notes on the sheet:
  //   contents of rom_1 (hex, n*v repeats v):
  //   210 60 251 70 3b2 251 70 3b2 251 70 3b2 251 70 3b2 251 70 3b2 251 70 3b2 251 70 3b2 251 160
endmodule

module ALU (
  input  [7:0] A,
  input  [7:0] B,
  input  Enable,
  input  Add_Sub,
  output [7:0] Output
);

  wire [7:0] demultiplexer_1_out0, demultiplexer_1_out1, multiplexer_1_out, xor_1_out;

  Demultiplexer #(.width(8)) demultiplexer_1 (
    .out0(demultiplexer_1_out0), .out1(demultiplexer_1_out1), .in(B), .sel(Add_Sub), .en(Enable));
  assign xor_1_out = demultiplexer_1_out1 ^ {8{1'b1}};  // XOR_Gate xor_1, 8 bits wide
  Multiplexer #(.width(8)) multiplexer_1 (
    .in0(demultiplexer_1_out0), .in1(xor_1_out), .out(multiplexer_1_out), .sel(Add_Sub), .en(Enable));
  Adder adder_1 (.a(A), .b(multiplexer_1_out), .out(Output), .cin(Add_Sub));  // open: cout
  Hex_Digit_Display hex_digit_display_1 (.value(Output[7:4]));  // open: dp
  Hex_Digit_Display hex_digit_display_2 (.value(Output[3:0]));  // open: dp

  // Notes on the sheet:
  //   demultiplexer
  //   block to turn number negative if mux and demux select bits are 1
  //   multiplexer
  //   8 bitAdder
  //   Output
endmodule

module PC (
  input  Enable,
  input  Clock,
  input  Reset,
  output [7:0] Output
);

  wire [7:0] adder_1_out;

  Register _8bit_Register (.D(adder_1_out), .en(Enable), .Q(Output), .clk(Clock), .clr(Reset));
  Adder adder_1 (.a(Output), .b(8'h1), .out(adder_1_out));  // open: cin, cout
endmodule

// REG
module register (
  input  [7:0] WriteData,
  input  [1:0] WriteReg,
  input  [1:0] ReadReg1,
  input  [1:0] ReadReg2,
  input  RegWrite,
  input  Clock,
  output [7:0] ReadData1,
  output [7:0] ReadData2
);

  wire and_1_out, and_2_out, and_3_out, and_4_out, decoder_1_out0, decoder_1_out1, decoder_1_out2,
       decoder_1_out3;
  wire [7:0] multiplexer_1_out, multiplexer_2_out, multiplexer_3_out, multiplexer_4_out, register_1_q,
       register_2_q, register_3_q, register_4_q;

  Decoder #(.select(2), .enable("false")) decoder_1 (
    .out0(decoder_1_out0), .out1(decoder_1_out1), .out2(decoder_1_out2), .out3(decoder_1_out3), .sel(WriteReg));
  and and_1 (and_1_out, decoder_1_out0, RegWrite);
  and and_2 (and_2_out, decoder_1_out1, RegWrite);
  and and_3 (and_3_out, decoder_1_out2, RegWrite);
  and and_4 (and_4_out, decoder_1_out3, RegWrite);
  Multiplexer #(.width(8), .enable("false")) multiplexer_1 (
    .in0(register_1_q), .in1(WriteData), .out(multiplexer_1_out), .sel(and_1_out));
  Multiplexer #(.width(8), .enable("false")) multiplexer_2 (
    .in0(register_2_q), .in1(WriteData), .out(multiplexer_2_out), .sel(and_2_out));
  Multiplexer #(.width(8), .enable("false")) multiplexer_3 (
    .in0(register_3_q), .in1(WriteData), .out(multiplexer_3_out), .sel(and_3_out));
  Multiplexer #(.width(8), .enable("false")) multiplexer_4 (
    .in0(register_4_q), .in1(WriteData), .out(multiplexer_4_out), .sel(and_4_out));
  Register register_1 (.D(multiplexer_1_out), .Q(register_1_q), .clk(Clock));  // open: en, clr
  Register register_2 (.D(multiplexer_2_out), .Q(register_2_q), .clk(Clock));  // open: en, clr
  Register register_3 (.D(multiplexer_3_out), .Q(register_3_q), .clk(Clock));  // open: en, clr
  Register register_4 (.D(multiplexer_4_out), .Q(register_4_q), .clk(Clock));  // open: en, clr
  Multiplexer #(.select(2), .width(8), .enable("false")) multiplexer_5 (
    .in0({8{1'b0}}), .in1(register_2_q), .in2(register_3_q), .in3(register_4_q), .out(ReadData1),
    .sel(ReadReg1));
  Multiplexer #(.select(2), .width(8), .enable("false")) multiplexer_6 (
    .in0({8{1'b0}}), .in1(register_2_q), .in2(register_3_q), .in3(register_4_q), .out(ReadData2),
    .sel(ReadReg2));

  // Notes on the sheet:
  //   Register File 8x8-bits
endmodule

module control (
  input  [11:0] \input ,
  output RegWrite__sw,
  output ALU___mem,
  output MemRead__lw,
  output Add_Sub,
  output ALUSrc,
  output [1:0] rs,
  output [1:0] rt,
  output [3:0] rd_offset_constant,
  output [1:0] destination,
  output MemWrite
);

  wire add_out, addi_out, not_1_out, not_2_out, not_3_out, not_4_out, not_5_out, not_6_out, not_7_out,
       not_8_out;
  wire [1:0] lw_addi_out;

  not not_1 (not_1_out, \input [9]);
  not not_2 (not_2_out, \input [10]);
  not not_3 (not_3_out, \input [8]);
  and and_1 (MemWrite, \input [8], not_1_out, not_2_out);
  not not_4 (not_4_out, \input [10]);
  not not_5 (not_5_out, \input [9]);
  not not_6 (not_6_out, \input [8]);
  not not_7 (not_7_out, \input [8]);
  and lw (MemRead__lw, not_4_out, not_5_out, not_6_out);
  and add (add_out, \input [9], \input [8]);
  and addi (addi_out, \input [9], not_7_out);
  or sub_add (lw_addi_out[1], \input [10], add_out);
  or or_1 (RegWrite__sw, not_3_out, \input [9]);
  Multiplexer #(.select(2), .width(2)) multiplexer_1 (
    .in0(\input [7:6]), .in1(\input [5:4]), .in2(\input [1:0]), .out(destination), .sel(lw_addi_out),
    .en(1'b1));  // open: in3
  or lw_addi (lw_addi_out[0], MemRead__lw, addi_out);
  or sub_add_addi (ALU___mem, \input [10], addi_out, add_out);
  not not_8 (not_8_out, RegWrite__sw);
  or lw_addi_sw (ALUSrc, not_8_out, lw_addi_out[0]);

  assign Add_Sub = \input [10];
  assign rd_offset_constant = \input [3:0];
  assign rs = \input [7:6];
  assign rt = \input [5:4];
endmodule
